# Fritzing sketch Dual 8-Bit Binary Counters (saved by Fritzing 0.9.2b)
breadboards: 1

parts:
  R17 = Resistor [tolerance=±5% resistance=220 package="2512 [SMD]"]
  LED11 = smd LED [color="Green (555nm)" package="0603 [SMD]"]
  R10 = Resistor [tolerance=±5% resistance=220 package="2512 [SMD]"]
  LED13 = smd LED [color="Green (555nm)" package="0603 [SMD]"]
  LED15 = smd LED [color="Green (555nm)" package="0603 [SMD]"]
  R11 = Resistor [tolerance=±5% resistance=220 package="2512 [SMD]"]
  Arduino_Board3 = Arduino Uno (Rev3) - ICSP
  LED17 = smd LED [color="Green (555nm)" package="0603 [SMD]"]
  R13 = Resistor [tolerance=±5% resistance=220 package="2512 [SMD]"]
  LED14 = smd LED [color="Green (555nm)" package="0603 [SMD]"]
  R12 = Resistor [tolerance=±5% resistance=220 package="2512 [SMD]"]
  R14 = Resistor [tolerance=±5% resistance=220 package="2512 [SMD]"]
  LED16 = smd LED [color="Green (555nm)" package="0603 [SMD]"]
  LED12 = smd LED [color="Green (555nm)" package="0603 [SMD]"]
  R16 = Resistor [tolerance=±5% resistance=220 package="2512 [SMD]"]
  IC2 = SHIFT REGISTER [package=dil16]
  LED10 = smd LED [color="Green (555nm)" package="0603 [SMD]"]
  R15 = Resistor [tolerance=±5% resistance=220 package="2512 [SMD]"]
  LED26 = smd LED [color="Red (633nm)" package="0805 [SMD]"]
  LED27 = smd LED [color="Red (633nm)" package="0805 [SMD]"]
  LED28 = smd LED [color="Red (633nm)" package="0805 [SMD]"]
  LED29 = smd LED [color="Red (633nm)" package="0805 [SMD]"]
  LED30 = smd LED [color="Red (633nm)" package="0805 [SMD]"]
  LED31 = smd LED [color="Red (633nm)" package="0805 [SMD]"]
  LED32 = smd LED [color="Red (633nm)" package="0805 [SMD]"]
  LED33 = smd LED [color="Red (633nm)" package="0805 [SMD]"]
  IC4 = SHIFT REGISTER [package=dil16]
  R27 = Resistor [tolerance=±5% resistance=220 package="2512 [SMD]"]
  R28 = Resistor [tolerance=±5% resistance=220 package="2512 [SMD]"]
  R29 = Resistor [tolerance=±5% resistance=220 package="2512 [SMD]"]
  R30 = Resistor [tolerance=±5% resistance=220 package="2512 [SMD]"]
  R31 = Resistor [tolerance=±5% resistance=220 package="2512 [SMD]"]
  R32 = Resistor [tolerance=±5% resistance=220 package="2512 [SMD]"]
  R33 = Resistor [tolerance=±5% resistance=220 package="2512 [SMD]"]
  R34 = Resistor [tolerance=±5% resistance=220 package="2512 [SMD]"]

nets:
  GND: R17.Pin_0, R10.Pin_0, R11.Pin_0, Arduino_Board3.GND, R13.Pin_0, R12.Pin_0, R14.Pin_0, R16.Pin_0, IC2.GND, IC2.G, R15.Pin_0, IC4.GND, IC4.SER, R27.Pin_0, R28.Pin_0, R29.Pin_0, R30.Pin_0, R31.Pin_0, R32.Pin_0, R33.Pin_0, R34.Pin_0
  N1: R17.Pin_1, LED16.cathode
  N2: LED11.cathode, R14.Pin_1
  N3: LED11.anode, IC2.QG
  N4: R10.Pin_1, LED10.cathode
  N5: LED13.cathode, R12.Pin_1
  N6: LED13.anode, IC2.QH
  N7: LED15.cathode, R15.Pin_1
  N8: LED15.anode, IC2.QC
  N9: R11.Pin_1, LED14.cathode
  N10: Arduino_Board3.ICSP_MISO, Arduino_Board3.D12/MISO, IC2.SCK, IC4.RCK
  N11: Arduino_Board3.D8, IC2.RCK, IC4.G
  N12: Arduino_Board3.D11_PWM/MOSI, IC2.SER
  VCC: Arduino_Board3.3V3, IC2.SCL, IC2.VCC, LED26.anode, IC4.QA, IC4.VCC
  N13: LED17.cathode, R13.Pin_1
  N14: LED17.anode, IC2.QB
  N15: LED14.anode, IC2.QE
  N16: LED16.anode, IC2.QF
  N17: LED12.cathode, R16.Pin_1
  N18: LED12.anode, IC2.QD
  N19: IC2.QA, LED10.anode
  N20: LED26.cathode, R33.Pin_1
  N21: LED27.cathode, R34.Pin_1
  N22: LED27.anode, IC4.QG
  N23: LED28.cathode, R28.Pin_1
  N24: LED28.anode, IC4.QF
  N25: LED29.cathode, R29.Pin_1
  N26: LED29.anode, IC4.QE
  N27: LED30.cathode, R31.Pin_1
  N28: LED30.anode, IC4.QD
  N29: LED31.cathode, R30.Pin_1
  N30: LED31.anode, IC4.QC
  N31: LED32.cathode, R32.Pin_1
  N32: LED32.anode, IC4.QB
  N33: LED33.cathode, R27.Pin_1
  N34: LED33.anode, IC4.QH
