# Fritzing sketch Interactive LED Chase Effect (saved by Fritzing 0.9.2b)
breadboards: 1

parts:
  Arduino_Board2 = Arduino Uno (Rev3) - ICSP
  LED1 = smd LED [color="Red (633nm)" package="0805 [SMD]"]
  R1 = Resistor [tolerance=±5% resistance=220 package="0603 [SMD]"]
  R2 = Resistor [tolerance=±5% resistance=220 package="0603 [SMD]"]
  R3 = Resistor [tolerance=±5% resistance=220 package="0603 [SMD]"]
  R4 = Resistor [tolerance=±5% resistance=220 package="0603 [SMD]"]
  R5 = Resistor [tolerance=±5% resistance=220 package="0603 [SMD]"]
  R6 = Resistor [tolerance=±5% resistance=220 package="0603 [SMD]"]
  R7 = Resistor [tolerance=±5% resistance=220 package="0603 [SMD]"]
  R8 = Resistor [tolerance=±5% resistance=220 package="0603 [SMD]"]
  R9 = Resistor [tolerance=±5% resistance=220 package="0603 [SMD]"]
  R10 = Resistor [tolerance=±5% resistance=220 package="0603 [SMD]"]
  LED2 = smd LED [color="Red (633nm)" package="0805 [SMD]"]
  LED3 = smd LED [color="Red (633nm)" package="0805 [SMD]"]
  LED4 = smd LED [color="Red (633nm)" package="0805 [SMD]"]
  LED5 = smd LED [color="Red (633nm)" package="0805 [SMD]"]
  LED6 = smd LED [color="Red (633nm)" package="0805 [SMD]"]
  LED7 = smd LED [color="Red (633nm)" package="0805 [SMD]"]
  LED8 = smd LED [color="Red (633nm)" package="0805 [SMD]"]
  LED9 = smd LED [color="Red (633nm)" package="0805 [SMD]"]
  LED10 = smd LED [color="Red (633nm)" package="0805 [SMD]"]
  U1 = POT [package=pot_mammoth]

nets:
  N1: Arduino_Board2.A2, U1.A
  N2: Arduino_Board2.GND, LED1.cathode, LED2.cathode, LED3.cathode, LED4.cathode, LED5.cathode, LED6.cathode, LED7.cathode, LED8.cathode, LED9.cathode, LED10.cathode, U1.E
  N3: Arduino_Board2.D8, R6.Pin_1
  N4: Arduino_Board2.D9_PWM, R5.Pin_1
  N5: Arduino_Board2.D10_PWM/SS, R4.Pin_1
  N6: Arduino_Board2.D11_PWM/MOSI, R3.Pin_1
  N7: Arduino_Board2.D12/MISO, R2.Pin_1
  N8: Arduino_Board2.D13/SCK, R1.Pin_1
  N9: Arduino_Board2.D4, R10.Pin_1
  N10: Arduino_Board2.D5_PWM, R9.Pin_1
  N11: Arduino_Board2.D6_PWM, R8.Pin_1
  N12: Arduino_Board2.D7, R7.Pin_1
  N13: Arduino_Board2.5V, U1.S
  N14: LED1.anode, R1.Pin_0
  N15: R2.Pin_0, LED2.anode
  N16: R3.Pin_0, LED3.anode
  N17: R4.Pin_0, LED4.anode
  N18: R5.Pin_0, LED5.anode
  N19: R6.Pin_0, LED6.anode
  N20: R7.Pin_0, LED7.anode
  N21: R8.Pin_0, LED8.anode
  N22: R9.Pin_0, LED9.anode
  N23: R10.Pin_0, LED10.anode
