# Fritzing sketch Interactive Traffic Lights (saved by Fritzing 0.9.2b)
breadboards: 1

parts:
  Part1 = Arduino Uno (Rev3) - ICSP
  LED1 = LED - 3mm [color="Red (633nm)" package="3 mm [THT]"]
  LED2 = LED - 3mm [color="Red (633nm)" package="3 mm [THT]"]
  S1 = Pushbutton [package="[THT]"]
  LED3 = LED - 3mm [color="Green (570nm)" package="3 mm [THT]"]
  LED4 = LED - 3mm [color="Green (570nm)" package="3 mm [THT]"]
  R1 = Resistor [tolerance=±5% resistance=220 package="0805 [SMD]"]
  R2 = Resistor [tolerance=±5% resistance=220 package="0805 [SMD]"]
  R3 = Resistor [tolerance=±5% resistance=220 package="0805 [SMD]"]
  R4 = Resistor [tolerance=±5% resistance=220 package="0805 [SMD]"]
  R5 = Resistor [tolerance=±5% resistance=220 package="0805 [SMD]"]
  R6 = Resistor [tolerance=±5% resistance=220 package="0805 [SMD]"]
  LED5 = LED - 3mm [color="Yellow (592nm)" package="3 mm [THT]"]

nets:
  N1: Part1.5V, S1.Pin_1, S1.Pin_2
  N2: Part1.ICSP_MOSI, Part1.D11_PWM/MOSI, R6.Pin_1
  N3: Part1.GND, LED1.cathode, LED2.cathode, LED3.cathode, LED4.cathode, R1.Pin_0, LED5.cathode
  N4: Part1.D8, R2.Pin_1
  N5: Part1.D9_PWM, R3.Pin_1
  N6: Part1.D10_PWM/SS, R5.Pin_1
  N7: Part1.D12/MISO, Part1.A4/SDA, R4.Pin_1
  N8: Part1.D2, S1.Pin_3, S1.Pin_4, R1.Pin_1
  N9: LED1.anode, R4.Pin_0
  N10: LED2.anode, R2.Pin_0
  N11: LED3.anode, R3.Pin_0
  N12: LED4.anode, R5.Pin_0
  N13: R6.Pin_0, LED5.anode
