# Fritzing sketch LED Flasher (saved by Fritzing 0.9.2b)
breadboards: 1

parts:
  Arduino_Board = Arduino Uno (Rev3) - ICSP
  LED1 = LED - 5mm [color="Red (633nm)" package="5 mm [THT]"]
  R1 = Resistor [tolerance=±5% resistance=150 package="2010 [SMD]"]

nets:
  N1: Arduino_Board.GND, R1.Pin_0
  N2: Arduino_Board.D10_PWM/SS, LED1.anode
  N3: LED1.cathode, R1.Pin_1
