# Fritzing sketch Light Sensor (saved by Fritzing 0.9.2b)
breadboards: 1

parts:
  Arduino_Board3 = Arduino Uno (Rev3) - ICSP
  R1 = Resistor [tolerance=±5% resistance=100 package=THT]
  R2 = Resistor [tolerance=±5% resistance=1.5k package=THT]
  R3 = Resistor [tolerance=±5% resistance=1.5k package=THT]
  R4 = Resistor [tolerance=±5% resistance=1.5k package=THT]
  LED1 = LED - 5mm [color="Green (555nm)" package="5 mm [THT]"]
  R5 = PHOTOCELL [package=photocell-kit]

nets:
  N1: Arduino_Board3.A0, R4.Pin_1, R5.P$1
  N2: Arduino_Board3.5V, R2.Pin_0
  N3: Arduino_Board3.GND, LED1.cathode, R5.P$2
  N4: Arduino_Board3.D6_PWM, R1.Pin_0
  N5: R1.Pin_1, LED1.anode
  N6: R2.Pin_1, R3.Pin_0
  N7: R3.Pin_1, R4.Pin_0
