# Fritzing sketch Mood Lamp (saved by Fritzing 0.9.2b)
breadboards: 1

parts:
  Arduino_Board2 = Arduino Uno (Rev3) - ICSP
  R1 = Resistor [tolerance=±5% resistance=220 package="0805 [SMD]"]
  R2 = Resistor [tolerance=±5% resistance=220 package="0805 [SMD]"]
  R3 = Resistor [tolerance=±5% resistance=220 package="0805 [SMD]"]
  LED1 = smd LED [color="Red (633nm)" package="1206 [SMD]"]
  LED2 = smd LED [color="Green (555nm)" package="1206 [SMD]"]
  LED3 = smd LED [color="Blue (430nm)" package="1206 [SMD]"]

nets:
  N1: Arduino_Board2.GND, LED1.cathode, LED2.cathode, LED3.cathode
  N2: Arduino_Board2.D9_PWM, R3.Pin_0
  N3: Arduino_Board2.D10_PWM/SS, R1.Pin_0
  N4: Arduino_Board2.D11_PWM/MOSI, R2.Pin_0
  N5: R1.Pin_1, LED2.anode
  N6: R2.Pin_1, LED1.anode
  N7: R3.Pin_1, LED3.anode
