# Fritzing sketch Piezo Sounder Melody Player (saved by Fritzing 0.9.2b)
breadboards: 1

parts:
  Arduino_Board3 = Arduino Uno (Rev3) - ICSP
  J2 = Screw terminal - 2 pins [package=THT]
  J3 = Piezo Speaker

nets:
  N1: Arduino_Board3.D9_PWM, J2.pin2, J3.pin2
  N2: Arduino_Board3.GND, J2.pin1, J3.pin1
