# Fritzing sketch Serial Temperature Sensor (saved by Fritzing 0.9.2b)
breadboards: 1

parts:
  Arduino_Board4 = Arduino Uno (Rev3) - ICSP
  T1 = LM35 Temperature Sensor [package="TO92 [THT]"]

nets:
  N1: Arduino_Board4.A0, T1.GND
  N2: Arduino_Board4.GND, T1.Vout
  N3: Arduino_Board4.5V, T1.+Vs
