# Fritzing sketch Shift Register 8-Bit Binary Counter (saved by Fritzing 0.9.2b)
breadboards: 1

parts:
  R17 = Resistor [tolerance=±5% resistance=220 package="2512 [SMD]"]
  LED11 = smd LED [color="Green (555nm)" package="0603 [SMD]"]
  R10 = Resistor [tolerance=±5% resistance=220 package="2512 [SMD]"]
  LED13 = smd LED [color="Green (555nm)" package="0603 [SMD]"]
  LED15 = smd LED [color="Green (555nm)" package="0603 [SMD]"]
  R11 = Resistor [tolerance=±5% resistance=220 package="2512 [SMD]"]
  Arduino_Board3 = Arduino Uno (Rev3) - ICSP
  LED17 = smd LED [color="Green (555nm)" package="0603 [SMD]"]
  R13 = Resistor [tolerance=±5% resistance=220 package="2512 [SMD]"]
  LED14 = smd LED [color="Green (555nm)" package="0603 [SMD]"]
  R12 = Resistor [tolerance=±5% resistance=220 package="2512 [SMD]"]
  R14 = Resistor [tolerance=±5% resistance=220 package="2512 [SMD]"]
  LED16 = smd LED [color="Green (555nm)" package="0603 [SMD]"]
  LED12 = smd LED [color="Green (555nm)" package="0603 [SMD]"]
  R16 = Resistor [tolerance=±5% resistance=220 package="2512 [SMD]"]
  IC2 = SHIFT REGISTER [package=dil16]
  LED10 = smd LED [color="Green (555nm)" package="0603 [SMD]"]
  R15 = Resistor [tolerance=±5% resistance=220 package="2512 [SMD]"]

nets:
  GND: R17.Pin_0, R10.Pin_0, R11.Pin_0, Arduino_Board3.GND, R13.Pin_0, R12.Pin_0, R14.Pin_0, R16.Pin_0, IC2.GND, IC2.G, R15.Pin_0
  N1: R17.Pin_1, LED16.cathode
  N2: LED11.cathode, R14.Pin_1
  N3: LED11.anode, IC2.QG
  N4: R10.Pin_1, LED10.cathode
  N5: LED13.cathode, R12.Pin_1
  N6: LED13.anode, IC2.QH
  N7: LED15.cathode, R15.Pin_1
  N8: LED15.anode, IC2.QC
  N9: R11.Pin_1, LED14.cathode
  N10: Arduino_Board3.D8, IC2.RCK
  N11: Arduino_Board3.D11_PWM/MOSI, IC2.SER
  N12: Arduino_Board3.D12/MISO, IC2.SCK
  3V3: Arduino_Board3.3V3, IC2.SCL, IC2.VCC
  N13: LED17.cathode, R13.Pin_1
  N14: LED17.anode, IC2.QB
  N15: LED14.anode, IC2.QE
  N16: LED16.anode, IC2.QF
  N17: LED12.cathode, R16.Pin_1
  N18: LED12.anode, IC2.QD
  N19: IC2.QA, LED10.anode
