# Fritzing sketch Traffic Lights (saved by Fritzing 0.9.2b)
breadboards: 1

parts:
  Arduino_Board1 = Arduino Uno (Rev3) - ICSP
  LED1 = smd LED [color="Red (633nm)" package="0603 [SMD]"]
  LED2 = smd LED [color="Red (633nm)" package="0603 [SMD]"]
  LED3 = smd LED [color="Red (633nm)" package="0603 [SMD]"]
  R1 = Resistor [tolerance=±5% resistance=220 package="2512 [SMD]"]
  R2 = Resistor [tolerance=±5% resistance=220 package="2512 [SMD]"]
  R3 = Resistor [tolerance=±5% resistance=220 package="2512 [SMD]"]

nets:
  N1: Arduino_Board1.D8, R3.Pin_0
  N2: Arduino_Board1.D9_PWM, R2.Pin_0
  N3: Arduino_Board1.D10_PWM/SS, R1.Pin_0
  N4: Arduino_Board1.D13/SCK, Arduino_Board1.GND, LED1.cathode, LED2.cathode, LED3.cathode
  N5: LED1.anode, R1.Pin_1
  N6: LED2.anode, R2.Pin_1
  N7: LED3.anode, R3.Pin_1
